# Fritzing sketch labo8 (saved by Fritzing 1.0.5)
breadboards: 3

parts:
  Mod1 = Raspberry Pi Pico W
  R1 = Resistor [tolerance=±5% power=0.25W resistance=1M package=THT]
  R2 = Resistor [tolerance=±5% power=0.25W resistance=220 package=THT]
  R3 = Resistor [tolerance=±5% power=0.25W resistance=4.7k package=THT]
  R4 = Rotary Potentiometer (Large) [maximum_resistance=10kΩ knob_status=50% power=0.5W package=THT]
  R5 = Resistor [tolerance=±5% power=0.25W resistance=10 package=THT]
  R6 = Resistor [tolerance=±5% power=0.25W resistance=220 package=THT]
  R7 = Resistor [tolerance=±5% power=0.25W resistance=1k package=THT]
  R8 = Rotary Potentiometer (Large) [maximum_resistance=10kΩ knob_status=50% power=0.5W package=THT]
  R9 = Resistor [tolerance=±5% power=0.25W resistance=1k package=THT]
  R10 = Resistor [tolerance=±5% power=0.25W resistance=1k package=THT]
  R11 = Rotary Potentiometer (Large) [maximum_resistance=10kΩ knob_status=50% power=0.5W package=THT]
  OLED_I2C1 = OLED 128x64 I2C Monochrome Display
  DHT1 = DHT22 Humidity and Temperature Sensor
  S1 = Pushbutton [package="[SMD]"]
  S2 = Pushbutton [package="[SMD]"]
  R12 = Resistor [tolerance=±1% power=0.25W resistance=2.2k package=THT]
  R13 = Resistor [tolerance=±1% power=0.25W resistance=2.2k package=THT]
  R14 = Resistor [tolerance=±1% power=0.25W resistance=1k package=THT]
  R15 = Resistor [tolerance=±1% power=0.25W resistance=1k package=THT]
  R16 = Resistor [tolerance=±1% power=0.25W resistance=1k package=THT]
  R17 = Resistor [tolerance=±1% power=0.25W resistance=1k package=THT]
  R18 = Resistor [tolerance=±1% power=0.25W resistance=1k package=THT]
  R19 = Resistor [tolerance=±1% power=0.25W resistance=1k package=THT]
  R20 = Resistor [tolerance=±1% power=0.25W resistance=1k package=THT]
  R21 = Resistor [tolerance=±1% power=0.25W resistance=1k package=THT]
  R22 = Resistor [tolerance=±1% power=0.25W resistance=2.2k package=THT]
  R23 = Resistor [tolerance=±1% power=0.25W resistance=2.2k package=THT]
  R24 = Resistor [tolerance=±1% power=0.25W resistance=2.2k package=THT]
  R25 = Resistor [tolerance=±1% power=0.25W resistance=2.2k package=THT]
  R26 = Resistor [tolerance=±1% power=0.25W resistance=2.2k package=THT]
  R27 = Resistor [tolerance=±1% power=0.25W resistance=2.2k package=THT]
  R28 = Resistor [tolerance=±1% power=0.25W resistance=2.2k package=THT]
  R29 = Resistor [tolerance=±1% power=0.25W resistance=1k package=THT]
  R30 = Resistor [tolerance=±1% power=0.25W resistance=2.2k package=THT]
  IC1 = LM324 [package=dil16]
  Mod2 = Raspberry Pi Pico W
  R31 = Resistor [tolerance=±1% power=0.25W resistance=2.2k package=THT]
  C1 = Tantalum Capacitor [capacitance=1μF voltage=35V package="100 mil [THT, tantalum]"]

nets:
  N1: Mod1.pin_1, DHT1.DATA
  GND: Mod1.pin_3, Mod1.pin_8, Mod1.pin_13, Mod1.pin_18, Mod1.pin_23, Mod1.pin_28, Mod1.pin_33, Mod1.pin_38, Mod1.pin_42, R1.Pin_0, R2.Pin_0, R4.leg1, R5.Pin_0, R8.leg1, R10.Pin_1, OLED_I2C1.GND, DHT1.GND, S1.Pin_1, S1.Pin_2, S2.Pin_1, S2.Pin_2, IC1.GND, Mod2.pin_3, Mod2.pin_8, Mod2.pin_13, Mod2.pin_18, Mod2.pin_23, Mod2.pin_28, Mod2.pin_33, Mod2.pin_38, Mod2.pin_42, C1.-
  N2: Mod1.pin_4, R12.Pin_1
  N3: Mod1.pin_5, R13.Pin_1
  N4: Mod1.pin_6, R22.Pin_1
  N5: Mod1.pin_7, R23.Pin_1
  N6: Mod1.pin_9, R24.Pin_1
  N7: Mod1.pin_10, R25.Pin_1
  N8: Mod1.pin_11, R26.Pin_1
  N9: Mod1.pin_12, R27.Pin_1
  N10: Mod1.pin_14, R29.Pin_1
  N11: Mod1.pin_15, R30.Pin_1
  N12: Mod1.pin_19, S2.Pin_3, S2.Pin_4
  N13: Mod1.pin_20, S1.Pin_3, S1.Pin_4
  N14: Mod1.pin_26, OLED_I2C1.SDA
  N15: Mod1.pin_27, OLED_I2C1.SCK
  N16: Mod1.pin_31, R3.Pin_0, R4.wiper
  N17: Mod1.pin_32, R7.Pin_1, R8.wiper
  N18: Mod1.pin_34, R10.Pin_0, R11.wiper
  N19: Mod1.pin_36, R4.leg2, R8.leg2, R9.Pin_1
  VDD: Mod1.pin_40, OLED_I2C1.VDD, DHT1.VDD
  N20: R1.Pin_1, R2.Pin_1, R3.Pin_1
  N21: R5.Pin_1, R6.Pin_0
  N22: R6.Pin_1, R7.Pin_0
  N23: R9.Pin_0, R11.leg1
  N24: R12.Pin_0, R14.Pin_0
  N25: R13.Pin_0, R14.Pin_1, R15.Pin_0
  N26: R15.Pin_1, R16.Pin_0, R22.Pin_0
  N27: R16.Pin_1, R17.Pin_0, R23.Pin_0
  N28: R17.Pin_1, R18.Pin_0, R24.Pin_0
  N29: R18.Pin_1, R19.Pin_0, R25.Pin_0
  N30: R19.Pin_1, R20.Pin_0, R26.Pin_0
  N31: R20.Pin_1, R21.Pin_0, R27.Pin_0
  N32: R21.Pin_1, R28.Pin_0, R29.Pin_0
  N33: R28.Pin_1, R30.Pin_0, IC1.IN2+
  N34: IC1.V+, Mod2.pin_40
  N35: IC1.IN2-, IC1.OUT2, R31.Pin_1
  N36: Mod2.pin_32, R31.Pin_0, C1.+

notes:
  Voltímetro
  Amperímetro
  Ohmetro
  Set
  Reset
  DHT22

custom parts:
  Raspberry Pi Pico W: Raspberry Pi Pico W. Based around the RP2040 microcontroller the Pico W is a low cost microcontroller device bringing Raspberry Pi quality, cost, and easy of use to the microcontroller space. The areas marked KEEPOUT in pcb silkscreen should not have traces running through them to avoid shorts on a soldered in module!
  LM324: LM324 Quad OpAmp

// code stored in the sketch: Untitled5.bas
# ============================================
# LAB 7 - MULTIMETRO DIGITAL (Volt + Amp + Ohm)
# Raspberry Pi Pico W - MicroPython
# GP26 (ADC0) -> Voltimetro  (divisor R3/R4)
# GP27 (ADC1) -> Amperimetro (shunt Ramp)
# GP28 (ADC2) -> Ohmetro
# ============================================

from machine import ADC, Pin
from utime import sleep

# --- CONFIGURACION ADC ---
adc_volt = ADC(26)   # GP26 = ADC Canal 0
adc_amp  = ADC(27)   # GP27 = ADC Canal 1
adc_ohm  = ADC(Pin(28)) # GP28 = ADC Canal 2

VREF         = 3.3
FACTOR_16    = VREF / 65535
NUM_MUESTRAS = 20

# --- RESISTENCIAS ---
# Voltimetro
R3 = 4700    # Resistencia serie (divisor)
R4 = 220     # Resistencia a GND (divisor)

# Amperimetro
RAMP = 10    # Shunt amperimetro (ohm)
R5   = 1000  # Carga
R6   = 220   # Proteccion GPIO

# Ohmetro
R7       = 1000  # Resistencia serie conocida (ohm)
RAMP_OHM = 1000  # Resistencia de medición para Ohmetro (ohm)

# --- FUNCIONES ---
def leer_promedio(adc):
    suma = 0
    for _ in range(NUM_MUESTRAS):
        suma += adc.read_u16()
    return suma / NUM_MUESTRAS

def leer_voltaje():
    promedio = leer_promedio(adc_volt)
    voltaje = promedio * FACTOR_16
    return voltaje

def leer_corriente():
    promedio = leer_promedio(adc_amp)
    v_shunt = promedio * FACTOR_16
    if v_shunt > 0.001:
        corriente_a  = v_shunt / RAMP
        corriente_ma = corriente_a * 1000
    else:
        corriente_ma = 0.0
    return corriente_ma

def leer_resistencia():
    promedio = leer_promedio(adc_ohm)
    v_ramp = promedio * FACTOR_16  # Voltaje sobre RAMP_OHM
    
    if v_ramp <= 0.0001:         # Circuito abierto
        return None
    
    # Corriente en el circuito
    I = v_ramp / RAMP_OHM
    
    # Resistencia desconocida
    rx = (VREF / I) - R7 - RAMP_OHM
    
    if rx < 0:
        return 0.0               # Cortocircuito o ruido
    return rx

# --- PROGRAMA PRINCIPAL (Ejecución plana) ---
print("=== MULTIMETRO DIGITAL (V + A + Ohm) ===")
print("GP26: Voltimetro | GP27: Amperimetro | GP28: Ohmetro")
print("-" * 65)

while True:
    # 1. Leer los tres valores
    voltaje = leer_voltaje()
    corriente_ma = leer_corriente()
    rx = leer_resistencia()

    # 2. Formatear la lectura de resistencia para la consola
    if rx is None:
        rx_str = "Abierto"
    elif rx < 1000:
        rx_str = f"{rx:.2f} ?"
    elif rx < 1_000_000:
        rx_str = f"{rx/1000:.3f} k?"
    else:
        rx_str = f"{rx/1_000_000:.3f} M?"

    # 3. Imprimir todo en una sola línea limpia
    print(f"Voltimetro: {voltaje:.4f} V | Amperimetro: {corriente_ma:.2f} mA | Ohmetro: {rx_str}")
    
    # Espera antes de la siguiente medición
    sleep(0.5)
